// Digital circuit bcu.dig as structural Verilog
module bcu (
  input  [2:0] BrOp,
  input  [63:0] A,
  input  [63:0] B,
  output taken
);

  wire BEQ_eq, BGE_eq, BGE_gt, BLT_lt, BNE_eq, not_1_out, or_1_out;

  Comparator #(.Bits(64)) BEQ (.a(A), .b(B), .eq(BEQ_eq));  // open: gt, lt
  Comparator #(.Bits(64)) BNE (.a(A), .b(B), .eq(BNE_eq));  // open: gt, lt
  Comparator #(.Bits(64), .Signed("true")) BLT (.a(A), .b(B), .lt(BLT_lt));  // open: gt, eq
  Comparator #(.Bits(64), .Signed("true")) BGE (.a(A), .b(B), .gt(BGE_gt), .eq(BGE_eq));  // open: lt
  or or_1 (or_1_out, BGE_gt, BGE_eq);
  Multiplexer #(.Selector_Bits(3)) multiplexer_1 (
    .sel(BrOp), .in_0(1'b0), .in_1(BEQ_eq), .in_2(not_1_out), .in_3(BLT_lt), .in_4(or_1_out), .in_5(1'b1),
    .in_6(1'b0), .in_7(1'b0), .out(taken));
  not not_1 (not_1_out, BNE_eq);
endmodule
