// Digital circuit inst-decoder.dig as structural Verilog
module inst_decoder (
  input  [31:0] IW,
  output [1:0] PCsel,
  output [2:0] ALUSrcB,
  output ALUSrcA,
  output [2:0] ALUOp,
  output RFW,
  output WDsel,
  output [2:0] BrOp
);

  wire ADDI_eq, ADDR_eq, BEQ_eq, BGE_eq, BLT_eq, BNE_eq, jal_eq_1_eq, jalr_eq_1_eq, LUI_eq, MUL_eq, SLLI_eq,
       SLLR_eq, SRLI_eq, SRLR_eq, SUB_eq;
  wire [3:0] priorityencoder_1_num;

  opcode_funct3_funct7_eq ADDR (
    .iw_opcode(IW[6:0]), .iw_funct3(IW[14:12]), .iw_funct7(IW[31:25]), .funct7({7{1'b0}}),
    .opcode(7'b0110011), .funct3(3'b000), .eq(ADDR_eq));
  opcode_funct3_funct7_eq SUB (
    .iw_opcode(IW[6:0]), .iw_funct3(IW[14:12]), .iw_funct7(IW[31:25]), .funct7(7'b0100000),
    .opcode(7'b0110011), .funct3(3'b000), .eq(SUB_eq));
  opcode_funct3_funct7_eq MUL (
    .iw_opcode(IW[6:0]), .iw_funct3(IW[14:12]), .iw_funct7(IW[31:25]), .funct7(7'b0000001),
    .opcode(7'b0110011), .funct3(3'b000), .eq(MUL_eq));
  opcode_funct3_eq SLLR (
    .iw_opcode(IW[6:0]), .iw_funct3(IW[14:12]), .funct3(3'b001), .opcode(7'b0110011), .eq(SLLR_eq));
  opcode_funct3_eq SRLR (
    .iw_opcode(IW[6:0]), .iw_funct3(IW[14:12]), .funct3(3'b101), .opcode(7'b0110011), .eq(SRLR_eq));
  opcode_funct3_eq ADDI (
    .iw_opcode(IW[6:0]), .iw_funct3(IW[14:12]), .funct3(3'b000), .opcode(7'b0010011), .eq(ADDI_eq));
  opcode_funct3_funct7_eq SLLI (
    .iw_opcode(IW[6:0]), .iw_funct3(IW[14:12]), .iw_funct7(IW[31:25]), .funct7({7{1'b0}}),
    .opcode(7'b0010011), .funct3(3'b001), .eq(SLLI_eq));
  opcode_funct3_funct7_eq SRLI (
    .iw_opcode(IW[6:0]), .iw_funct3(IW[14:12]), .iw_funct7(IW[31:25]), .funct7({7{1'b0}}),
    .opcode(7'b0010011), .funct3(3'b101), .eq(SRLI_eq));
  opcode_funct3_eq BEQ (.iw_opcode(IW[6:0]), .iw_funct3(IW[14:12]), .funct3(3'b000), .opcode(7'b1100011), .eq(BEQ_eq));
  opcode_funct3_eq BNE (.iw_opcode(IW[6:0]), .iw_funct3(IW[14:12]), .funct3(3'b001), .opcode(7'b1100011), .eq(BNE_eq));
  opcode_funct3_eq BLT (.iw_opcode(IW[6:0]), .iw_funct3(IW[14:12]), .funct3(3'b100), .opcode(7'b1100011), .eq(BLT_eq));
  opcode_funct3_eq BGE (.iw_opcode(IW[6:0]), .iw_funct3(IW[14:12]), .funct3(3'b101), .opcode(7'b1100011), .eq(BGE_eq));
  jal_eq jal_eq_1 (.opcode(IW[6:0]), .eq(jal_eq_1_eq));
  Comparator #(.Bits(7)) LUI (.a(IW[6:0]), .b(7'b0110111), .eq(LUI_eq));  // open: gt, lt
  jalr_eq jalr_eq_1 (.opcode(IW[6:0]), .funct3(IW[14:12]), .eq(jalr_eq_1_eq));
  PriorityEncoder #(.Selector_Bits(4)) priorityencoder_1 (
    .in0(ADDR_eq), .in1(SUB_eq), .in2(MUL_eq), .in3(SLLR_eq), .in4(SRLR_eq), .in5(ADDI_eq), .in6(SLLI_eq),
    .in7(SRLI_eq), .in8(BEQ_eq), .in9(BNE_eq), .in10(BLT_eq), .in11(BGE_eq), .in12(LUI_eq),
    .in13(jal_eq_1_eq), .in14(jalr_eq_1_eq), .in15(1'b0), .num(priorityencoder_1_num));  // open: any
  ROM #(.AddrBits(4), .Bits(14)) rom_1 (
    .A(priorityencoder_1_num), .sel(1'b1), .D({WDsel, RFW, BrOp, ALUSrcB, ALUSrcA, ALUOp, PCsel}));

  // Notes on the sheet:
  //   contents of rom_1 (hex, n*v repeats v):
  //   3000,3004,3008,300c,3010,3040,304c,3050,22e1,24e1,26e1,28e1,311c
  //   ,1b61,1a41
endmodule
